# Fritzing sketch tablet_timer (saved by Fritzing 0.9.3b)
breadboards: 1

parts:
  Part1 = HUZZAH ESP8266 Breakout
  7SEG1 = 7-Segment LED I2C Backpack (blue)
  Part2 = RFID-RC522-v3
  S1 = Pushbutton [package=THT]
  R1 = Resistor [tolerance=±5% resistance=10k package="0805 [SMD]"]
  JACK1 = 2.1mm Barrel Jack with Terminal Block
  USBTTL1 = USB TTL Serial Cable
  J1 = Piezo Speaker
  R2 = Resistor [tolerance=±5% resistance=100 package=THT]

nets:
  N1: Part1.TXD, USBTTL1.RX
  N2: Part1.RXD_5V, USBTTL1.TX
  N3: Part1.VIN, 7SEG1.V+, JACK1.POS
  GND: Part1.GND, 7SEG1.GND, Part2.GND, R1.Pin_0, JACK1.NEG, USBTTL1.GND, J1.pin1
  N4: Part1.GPIO16, S1.leg1, R1.Pin_1
  N5: Part1.GPIO14, Part2.SCK
  N6: Part1.GPIO12, Part2.MISO
  N7: Part1.GPIO13, Part2.MOSI
  3.3V: Part1.3.3V, Part2.3.3V, S1.leg0
  N8: Part1.GPIO15, R2.Pin_1
  N9: Part1.GPIO2, Part2.SDA
  N10: Part1.GPIO0, Part2.RST
  N11: Part1.GPIO4, 7SEG1.SDA
  N12: Part1.GPIO5, 7SEG1.SCL
  N13: J1.pin2, R2.Pin_0

notes:
  5V
  3.3V
  GND
  Tablet Timer Project
  5v Power Supply
  https://github.com/AnykeyNL/IpadTimer
  Serial connector
  for programming
  100 Ohm
  10K Ohm
  Switch

custom parts:
  HUZZAH ESP8266 Breakout: The ESP8266 processor from Espressif is an 80 MHz microcontroller with a full WiFi front-end (both as client and access point) and TCP/IP stack with DNS support as well.
  7-Segment LED I2C Backpack (blue): 4-digit, 7-segment LED Display with I2C Control
  RFID-RC522-v3: A simple China made RFID-RC522 Reader (6x4 cm); do check the pin labels, as this is a MFRC522 based clone.
